// Logisim project cpu-harness.circ as structural Verilog: 1 circuit, main circuit main
module main (
  output [15:0] r0,
  output [15:0] r1,
  output [15:0] r2,
  output [15:0] r3,
  output [15:0] d0,
  output [15:0] d1,
  output [15:0] Data_Mem_Data,
  output [15:0] Data_Mem_Addr,
  output Write_Enabled,
  output [15:0] Clock_Count
);

  wire clock_1_out;
  wire [15:0] adder_1_out, main_1_data_mem_addr, main_1_data_mem_data, main_1_to_instr_mem, ram_1_data;

  // Probe on main_1_to_instr_mem
  // Probe on r0
  // Probe on r1
  // Probe on r2
  // Probe on r3
  // Probe on ram_1_data
  RAM #(.addrWidth(16), .dataWidth(16)) ram_1 (
    .addr(main_1_to_instr_mem), .data(ram_1_data));  // open: sel, clk, ld, clr
  cpu_main main_1 (
    .From_Instr_Mem(ram_1_data), .r0(r0), .r1(r1), .r2(r2), .r3(r3), .Display_0(d0), .Display_1(d1),
    .clk(clock_1_out), .To_Instr_Mem(main_1_to_instr_mem), .Data_Mem_Data(main_1_data_mem_data),
    .Data_Mem_Addr(main_1_data_mem_addr), .Data_Mem_Write(Write_Enabled));
  Multiplexer #(.width(16), .enable("false")) multiplexer_1 (
    .in0({16{1'b0}}), .in1(main_1_data_mem_data), .out(Data_Mem_Data), .sel(Write_Enabled));
  Multiplexer #(.width(16), .enable("false")) multiplexer_2 (
    .in0({16{1'b0}}), .in1(main_1_data_mem_addr), .out(Data_Mem_Addr), .sel(Write_Enabled));
  Clock clock_1 (.out(clock_1_out));
  // Probe on d0
  // Probe on d1
  Register #(.width(16)) register_1 (.D(adder_1_out), .Q(Clock_Count), .clk(clock_1_out));  // open: en, clr
  Adder #(.width(16)) adder_1 (.a(16'h1), .b(Clock_Count), .out(adder_1_out));  // open: cin, cout

  // Notes on the sheet:
  //   Instruction Memory
  //   YOUR CPU SHOULD FIT OVER THERE
  //   There should be no blue/red wires here, and nothing should be x's.
  //   If you want to test your code, you can do it here by right clicking the RAM (Instruction Memory) and load image the appropriate hex file
endmodule
