// Logisim project cpu.circ as structural Verilog: 5 circuits, main circuit main
module main (
  input  [15:0] From_Instr_Mem,
  input  clk,
  output [15:0] r0,
  output [15:0] r1,
  output [15:0] r2,
  output [15:0] r3,
  output [15:0] Display_0,
  output [15:0] Display_1,
  output [15:0] To_Instr_Mem,
  output [15:0] Data_Mem_Data,
  output [15:0] Data_Mem_Addr,
  output Data_Mem_Write
);

  wire adder_2_cout, ALUSrc, and_1_out, and_2_out, beq, bne, Branch, d0_t, d1_t, Disp, ExtOp, j, jal, jr,
       lui, main_2_equal, main_2_signed_overflow, MemtoReg, nop, not_1_out, not_2_out, or_3_out, RegDst,
       RegWrite;
  wire [1:0] multiplexer_1_out, multiplexer_2_out, rd, rs, rt;
  wire [3:0] ALUCtrl, opcode;
  wire [5:0] funct;
  wire [7:0] imm;
  wire [11:0] address;
  wire [15:0] adder_1_out, adder_2_out, DataOut, demultiplexer_1_out0, demultiplexer_1_out1, jraddress,
       main_1_read_data_1, multiplexer_3_out, multiplexer_4_out, multiplexer_5_out, multiplexer_6_out,
       multiplexer_7_out, multiplexer_8_out, multiplexer_9_out, multiplexer_10_out, multiplexer_11_out,
       multiplexer_12_out, multiplexer_13_out, multiplexer_14_out, offset, register_1_q, shifter_1_out;

  Multiplexer #(.width(2)) multiplexer_1 (.in0(rt), .in1(rd), .out(multiplexer_1_out), .sel(RegDst));  // open: en
  Multiplexer #(.width(2)) multiplexer_2 (
    .in0(multiplexer_1_out), .in1(2'b11), .out(multiplexer_2_out), .sel(jal));  // open: en
  Multiplexer #(.width(16)) multiplexer_3 (
    .in0(multiplexer_4_out), .in1(To_Instr_Mem), .out(multiplexer_3_out), .sel(jal));  // open: en
  Multiplexer #(.width(16)) multiplexer_4 (
    .in0(multiplexer_5_out), .in1(shifter_1_out), .out(multiplexer_4_out), .sel(lui));  // open: en
  Multiplexer #(.width(16)) multiplexer_5 (
    .in0(Data_Mem_Addr), .in1(DataOut), .out(multiplexer_5_out), .sel(MemtoReg));  // open: en
  or or_1 (nop, Branch, j, jal, jr);
  Regfile_main main_1 (
    .Read_register_1(rs), .Read_register_2(rt), .write_register(multiplexer_2_out),
    .write_data(multiplexer_3_out), .Reg_0_Value(r0), .Reg_1_Value(r1), .Reg_2_Value(r2), .Reg_3_Value(r3),
    .RegWrite(RegWrite), .clock(clk), .Read_Data_1(main_1_read_data_1), .Read_Data_2(Data_Mem_Data));
  extender extender_1 (.in_1(imm), .in_2(ExtOp), .out_3(offset));
  Multiplexer #(.width(16)) multiplexer_6 (
    .in0(From_Instr_Mem), .in1(16'h6), .out(multiplexer_6_out), .sel(nop));  // open: en
  Register #(.width(16)) register_1 (.D(multiplexer_6_out), .Q(register_1_q), .clk(clk));  // open: en, clr
  Multiplexer #(.width(16)) multiplexer_7 (
    .in0(Data_Mem_Data), .in1(offset), .out(multiplexer_7_out), .sel(ALUSrc));  // open: en
  Shifter #(.width(16)) shifter_1 (.in(offset), .\dist (4'b1000), .out(shifter_1_out));
  instructionSplitter instructionsplitter_1 (
    .in_1(register_1_q), .func(funct), .rd(rd), .rt(rt), .rs(rs), .opcode(opcode), .imm(imm),
    .address(address));
  assign jraddress = jr ? main_1_read_data_1 : 16'bz;  // Controlled_Buffer controlled_buffer_1
  alu_main main_2 (
    .Switch__S(ALUCtrl), .X(main_1_read_data_1), .Equal(main_2_equal), .RESULT(Data_Mem_Addr),
    .Signed_Overflow(main_2_signed_overflow), .Y(multiplexer_7_out));
  not not_1 (not_1_out, main_2_equal);
  LED led_1 (.in(main_2_signed_overflow));
  and and_1 (and_1_out, main_2_equal, beq);
  and and_2 (and_2_out, not_1_out, bne);
  control control_1 (
    .in_1(opcode), .in_2(funct), .out_3(RegDst), .out_4(MemtoReg), .out_5(Data_Mem_Write), .out_6(ALUCtrl),
    .out_7(ALUSrc), .out_8(ExtOp), .out_9(RegWrite), .out_10(Disp), .out_11(lui), .out_12(beq), .out_13(bne),
    .out_14(j), .out_15(jal), .out_16(jr));
  or or_2 (Branch, and_1_out, and_2_out);
  Register #(.width(16)) register_2 (.D(multiplexer_13_out), .Q(To_Instr_Mem), .clk(clk));  // open: en, clr
  assign DataOut = Data_Mem_Write ? Data_Mem_Data : 16'bz;  // Controlled_Buffer controlled_buffer_2
  RAM #(.addrWidth(16), .dataWidth(16)) ram_1 (
    .addr(Data_Mem_Addr), .data(DataOut), .sel(1'b1), .clk(clk), .ld(not_2_out));  // open: clr
  not not_2 (not_2_out, Data_Mem_Write);
  Adder #(.width(16)) adder_1 (.a(To_Instr_Mem), .b(16'h1), .out(adder_1_out));  // open: cin, cout
  Multiplexer #(.width(16)) multiplexer_8 (
    .in0(adder_1_out), .in1(To_Instr_Mem), .out(multiplexer_8_out), .sel(Branch));  // open: en
  Adder #(.width(16)) adder_2 (.a(multiplexer_8_out), .b(offset), .out(adder_2_out), .cout(adder_2_cout));  // open: cin
  Demultiplexer #(.width(16)) demultiplexer_1 (
    .out0(demultiplexer_1_out0), .out1(demultiplexer_1_out1), .in(multiplexer_9_out), .sel(imm[0]));  // open: en
  Multiplexer #(.select(2), .width(16)) multiplexer_9 (
    .in0(r0), .in1(r1), .in2(r2), .in3(r3), .out(multiplexer_9_out), .sel(rs));  // open: en
  Multiplexer #(.width(16)) multiplexer_10 (
    .in0(multiplexer_8_out), .in1(adder_2_out), .out(multiplexer_10_out), .sel(Branch));  // open: en
  Demultiplexer demultiplexer_2 (.out0(d0_t), .out1(d1_t), .in(Disp), .sel(imm[0]));  // open: en
  Multiplexer #(.width(16)) multiplexer_11 (
    .in0(multiplexer_10_out), .in1({To_Instr_Mem[15:12], address}), .out(multiplexer_11_out), .sel(or_3_out));  // open: en
  or or_3 (or_3_out, jal, j);
  Multiplexer #(.width(16)) multiplexer_12 (
    .in0(Display_0), .in1(demultiplexer_1_out0), .out(multiplexer_12_out), .sel(d0_t));  // open: en
  Multiplexer #(.width(16)) multiplexer_13 (
    .in0(multiplexer_11_out), .in1(jraddress), .out(multiplexer_13_out), .sel(jr));  // open: en
  Hex_Digit_Display hex_digit_display_1 (.value(Display_0[15:12]));  // open: dp
  Hex_Digit_Display hex_digit_display_2 (.value(Display_0[11:8]));  // open: dp
  Register #(.width(16)) register_3 (.D(multiplexer_12_out), .Q(Display_0), .clk(clk));  // open: en, clr
  Hex_Digit_Display hex_digit_display_3 (.value(Display_0[7:4]));  // open: dp
  Hex_Digit_Display hex_digit_display_4 (.value(Display_0[3:0]));  // open: dp
  Hex_Digit_Display hex_digit_display_5 (.value(Display_1[15:12]));  // open: dp
  Multiplexer #(.width(16)) multiplexer_14 (
    .in0(Display_1), .in1(demultiplexer_1_out1), .out(multiplexer_14_out), .sel(d1_t));  // open: en
  Hex_Digit_Display hex_digit_display_6 (.value(Display_1[7:4]));  // open: dp
  Hex_Digit_Display hex_digit_display_7 (.value(Display_1[11:8]));  // open: dp
  Register #(.width(16)) register_4 (.D(multiplexer_14_out), .Q(Display_1), .clk(clk));  // open: en, clr
  Hex_Digit_Display hex_digit_display_8 (.value(Display_1[3:0]));  // open: dp

  // Other names for the same wires on the sheet: ALUOut[15:0] = Data_Mem_Addr; currPC[15:0] = To_Instr_Mem;
  //   d0[15:0] = Display_0; d1[15:0] = Display_1; DataIn[15:0] = Data_Mem_Data; MemWrite = Data_Mem_Write

  // Notes on the sheet:
  //   This is the instruction that you would receive as INPUT
  //   This is the current PC that you need to send as OUTPUT
  //   INSTRUCTION FETCH/CONTROL
  //   This is a CLK that is an INPUT driven from the harness.
  //   Remember, this circuit is loaded from the harness to be tested!
  //   DO NOT CHANGE THE LOCATIONS OF THE INPUTS OR OUTPUTS! IF YOU DO SO, YOU NEED TO MAKE SURE THE PINS ARE IN THE RIGHT PLACES!
  //   INSTRUCTION EXECUTION
  //   These are OUTPUTS of the circuit
  //   MEMORY
  //   DISPLAY
  //   calulate currPC
  //   These are OUTPUTS of the circuit
endmodule

module memory (
  input  [15:0] Detain,
  input  [15:0] Address,
  input  MemWrite,
  output [15:0] DataOut,
  output clk
);

  wire not_1_out;

  assign DataOut = MemWrite ? Detain : 16'bz;  // Controlled_Buffer controlled_buffer_1
  not not_1 (not_1_out, MemWrite);
  RAM #(.addrWidth(16), .dataWidth(16)) ram_1 (
    .addr(Address), .data(DataOut), .sel(1'b1), .clk(clk), .ld(not_1_out));  // open: clr
endmodule

module control (
  input  [3:0] in_1,
  input  [5:0] in_2,
  output out_3,
  output out_4,
  output out_5,
  output [3:0] out_6,
  output out_7,
  output out_8,
  output out_9,
  output out_10,
  output out_11,
  output out_12,
  output out_13,
  output out_14,
  output out_15,
  output out_16
);

  wire ADD, ADDI, ADDP8, AND, and_14_out, and_15_out, and_16_out, and_17_out, and_18_out, and_19_out,
       and_20_out, and_21_out, and_22_out, and_23_out, ANDI, not_1_out, not_2_out, not_3_out, not_4_out,
       not_5_out, not_6_out, not_7_out, not_8_out, not_9_out, not_10_out, OR, or_1_out, or_2_out, or_3_out,
       ORI, SLLV, SLT, SRAV, SRLV, SUB, SUBP8;

  not not_1 (not_1_out, in_1[2]);
  not not_2 (not_2_out, in_1[3]);
  not not_3 (not_3_out, in_1[1]);
  not not_4 (not_4_out, in_1[0]);
  and and_1 (out_3, not_2_out, not_1_out, not_3_out, not_4_out);
  and and_2 (out_15, not_2_out, not_1_out, not_3_out, in_1[0]);
  and and_3 (out_14, not_2_out, not_1_out, in_1[1], not_4_out);
  and and_4 (out_16, not_2_out, not_1_out, in_1[1], in_1[0]);
  and and_5 (out_12, not_2_out, in_1[2], not_3_out, not_4_out);
  and and_6 (ADDI, not_2_out, in_1[2], not_3_out, in_1[0]);
  and and_7 (ANDI, not_2_out, in_1[2], in_1[1], not_4_out);
  and and_8 (ORI, not_2_out, in_1[2], in_1[1], in_1[0]);
  and and_9 (out_13, in_1[3], not_1_out, not_3_out, not_4_out);
  and and_10 (out_5, in_1[3], not_1_out, not_3_out, in_1[0]);
  and and_11 (out_11, in_1[3], not_1_out, in_1[1], not_4_out);
  and and_12 (out_4, in_1[3], not_1_out, in_1[1], in_1[0]);
  and and_13 (out_10, in_1[3], in_1[2], not_3_out, not_4_out);
  not not_5 (not_5_out, in_2[4]);
  not not_6 (not_6_out, in_2[5]);
  not not_7 (not_7_out, in_2[3]);
  not not_8 (not_8_out, in_2[1]);
  not not_9 (not_9_out, in_2[2]);
  not not_10 (not_10_out, in_2[0]);
  and and_14 (and_14_out, not_6_out, not_5_out, not_7_out, not_9_out, not_8_out, not_10_out);
  and and_15 (and_15_out, not_6_out, not_5_out, not_7_out, not_9_out, not_8_out, in_2[0]);
  and and_16 (and_16_out, not_6_out, not_5_out, not_7_out, not_9_out, in_2[1], not_10_out);
  and and_17 (and_17_out, not_6_out, not_5_out, not_7_out, not_9_out, in_2[1], in_2[0]);
  and and_18 (and_18_out, not_6_out, not_5_out, not_7_out, in_2[2], not_8_out, not_10_out);
  and and_19 (and_19_out, not_6_out, not_5_out, not_7_out, in_2[2], not_8_out, in_2[0]);
  and and_20 (and_20_out, not_6_out, not_5_out, not_7_out, in_2[2], in_2[1], not_10_out);
  and and_21 (and_21_out, not_6_out, not_5_out, not_7_out, in_2[2], in_2[1], in_2[0]);
  and and_22 (and_22_out, not_6_out, not_5_out, in_2[3], not_7_out, not_9_out, not_10_out);
  and and_23 (and_23_out, not_6_out, not_5_out, in_2[3], not_9_out, not_8_out, in_2[0]);
  and and_24 (ADD, and_14_out, out_3);
  and and_25 (SUB, and_15_out, out_3);
  and and_26 (SLLV, and_16_out, out_3);
  and and_27 (SRLV, and_17_out, out_3);
  and and_28 (SRAV, and_18_out, out_3);
  and and_29 (SLT, and_19_out, out_3);
  and and_30 (OR, and_20_out, out_3);
  and and_31 (AND, and_21_out, out_3);
  and and_32 (ADDP8, and_22_out, out_3);
  and and_33 (SUBP8, and_23_out, out_3);
  or or_1 (or_1_out, ADD, ADDI, out_4, out_5);
  assign out_6 = or_1_out ? 4'b0000 : 4'bz;  // Controlled_Buffer controlled_buffer_1
  assign out_6 = SUB ? 4'b0001 : 4'bz;  // Controlled_Buffer controlled_buffer_2
  assign out_6 = SLLV ? 4'b0010 : 4'bz;  // Controlled_Buffer controlled_buffer_3
  assign out_6 = SRLV ? 4'b0011 : 4'bz;  // Controlled_Buffer controlled_buffer_4
  assign out_6 = SRAV ? 4'b0100 : 4'bz;  // Controlled_Buffer controlled_buffer_5
  assign out_6 = SLT ? 4'b0101 : 4'bz;  // Controlled_Buffer controlled_buffer_6
  assign out_6 = or_2_out ? 4'b0110 : 4'bz;  // Controlled_Buffer controlled_buffer_7
  or or_2 (or_2_out, ORI, OR);
  assign out_6 = or_3_out ? 4'b0111 : 4'bz;  // Controlled_Buffer controlled_buffer_8
  or or_3 (or_3_out, AND, ANDI);
  assign out_6 = ADDP8 ? 4'b1000 : 4'bz;  // Controlled_Buffer controlled_buffer_9
  assign out_6 = SUBP8 ? 4'b1001 : 4'bz;  // Controlled_Buffer controlled_buffer_10
  or or_4 (out_7, ADDI, ANDI, ORI, out_5, out_11, out_4, out_10);
  or or_5 (out_8, ADDI, out_12, out_13, out_5, out_4);
  or or_6 (out_9, out_3, ADDI, ANDI, ORI, out_11, out_4, out_15);

  // Other names for the same wires on the sheet: ALUctrl[3:0] = out_6; ALUsrc = out_7; BEQ = out_12; BNE = out_13;
  //   DISP = out_10; ExtOp = out_8; funct[5:0] = in_2; J = out_14; JAL = out_15; JR = out_16; LUI = out_11;
  //   LW = out_4; MemtoReg = out_4; opcode[3:0] = in_1; RegDst = out_3; RTYPE = out_3; RegWrite = out_9;
  //   MemWrite = out_5; SW = out_5
endmodule

module instructionSplitter (
  input  [15:0] in_1,
  output [5:0] func,
  output [1:0] rd,
  output [1:0] rt,
  output [1:0] rs,
  output [3:0] opcode,
  output [7:0] imm,
  output [11:0] address
);


  assign address = in_1[11:0];
  assign func = in_1[5:0];
  assign imm = in_1[7:0];
  assign opcode = in_1[15:12];
  assign rd = in_1[7:6];
  assign rs = in_1[11:10];
  assign rt = in_1[9:8];
endmodule

module extender (
  input  [7:0] in_1,
  input  in_2,
  output [15:0] out_3
);

  wire [15:0] bit_extender_1_out, bit_extender_2_out;

  assign bit_extender_1_out = {{8{1'b0}}, in_1};  // Bit_Extender bit_extender_1
  assign bit_extender_2_out = {{8{in_1[7]}}, in_1};  // Bit_Extender bit_extender_2
  Multiplexer #(.width(16)) multiplexer_1 (
    .in0(bit_extender_1_out), .in1(bit_extender_2_out), .out(out_3), .sel(in_2));  // open: en
endmodule
