// Logisim project alu.circ as structural Verilog: 1 circuit, main circuit main
module main (
  input  [15:0] X,
  input  [15:0] Y,
  input  [3:0] switch__S,
  output signed_overflow,
  output [15:0] result,
  output equal
);


  // Notes on the sheet:
  //   These are INPUTS to your circuit
  //   This is an INPUT to your circuit
  //   DO NOT CHANGE THE LOCATIONS OF THE INPUTS/OUTPUTS! IF YOU DO SO, YOU NEED TO MAKE SURE THE PINS ARE AT THE RIGHT PLACE!
  //   These are OUTPUTS to your circuit
endmodule
